# Fritzing sketch Robotic Arm (saved by Fritzing 0.8.7b)
circuit board: 4.68405cm x 6.82476cm
breadboards: 1

parts:
  D11 = female pin header, 3 pins [form="♀ (female)"]
  D10 = female pin header, 3 pins [form="♀ (female)"]
  D9 = female pin header, 3 pins [form="♀ (female)"]
  D6 = female pin header, 3 pins [form="♀ (female)"]
  D5 = female pin header, 3 pins [form="♀ (female)"]
  D3 = female pin header, 3 pins [form="♀ (female)"]
  Nano = Arduino Nano (Rev3.0)
  SW = female pin header, 2 pins [form="♀ (female)"]
  5V = female pin header, 2 pins [form="♀ (female)"]
  5V_GND_TX_RX = Generic female header - 4 pins [form="♀ (female)" package=THT]
  JMP = female pin header, 3 pins [form="♀ (female)"]
  C1 = Electrolytic Capacitor [capacitance=4.7mF voltage=20V package="300 mil [THT, electrolytic]"]

nets:
  N1: D11.pin1, Nano.D11/MOSI
  N2: D11.pin2, D10.pin2, D9.pin2, D6.pin2, D5.pin2, D3.pin2, JMP.pin2, C1.+
  GND: D11.pin3, D10.pin3, D9.pin3, D6.pin3, D5.pin3, D3.pin3, Nano.GND, 5V.pin2, 5V_GND_TX_RX.GND, C1.-
  N3: D10.pin1, Nano.D10
  N4: D9.pin1, Nano.D9
  N5: D6.pin1, Nano.D6
  N6: D5.pin1, Nano.D5
  N7: D3.pin1, Nano.D3
  N8: Nano.D7, 5V_GND_TX_RX.RXD
  N9: Nano.D8, 5V_GND_TX_RX.TXD
  VIN: Nano.VIN, SW.pin1, 5V_GND_TX_RX.VCC, JMP.pin1
  N10: Nano.5V, JMP.pin3
  N11: SW.pin2, 5V.pin1

notes:
  [5-DoF] Robotic Arm (Arduino Based)

custom parts:
  Generic female header - 4 pins: Generic female header
